// Logisim project Decoder Project simult.circ as structural Verilog: 1 circuit, main circuit main
module main (
  input  A,
  input  B,
  input  C
);

  wire decoder_1_out0, decoder_1_out1, decoder_1_out2, decoder_1_out3, decoder_1_out4, decoder_1_out5,
       decoder_1_out6, decoder_1_out7, or_1_out, or_2_out, or_3_out, or_4_out, or_5_out, or_6_out;

  Decoder #(.select(3)) decoder_1 (
    .out0(decoder_1_out0), .out1(decoder_1_out1), .out2(decoder_1_out2), .out3(decoder_1_out3),
    .out4(decoder_1_out4), .out5(decoder_1_out5), .out6(decoder_1_out6), .out7(decoder_1_out7),
    .sel({A, B, C}));  // open: en
  or or_1 (or_1_out, decoder_1_out0, decoder_1_out1, decoder_1_out2, decoder_1_out3, decoder_1_out4, decoder_1_out7);
  or or_2 (or_2_out, decoder_1_out3, decoder_1_out4, decoder_1_out5, decoder_1_out7);
  or or_3 (or_3_out, decoder_1_out1, decoder_1_out4, decoder_1_out5, decoder_1_out7);
  or or_4 (or_4_out, decoder_1_out0, decoder_1_out2, decoder_1_out3);
  or or_5 (or_5_out, decoder_1_out0, decoder_1_out1, decoder_1_out2, decoder_1_out7);
  or or_6 (or_6_out, decoder_1_out1, decoder_1_out2, decoder_1_out3, decoder_1_out4, decoder_1_out6, decoder_1_out7);
  _7_Segment_Display u_7_segment_display_1 (
    .g(or_6_out), .f(or_5_out), .a(or_1_out), .b(or_2_out), .e(or_4_out), .d(or_1_out), .c(or_3_out));  // open: dp

  // Notes on the sheet:
  //   ( MSB )
  //   ( LSB )
  //   b
  //   c
  //   e
  //   f
  //   g
  //   a  ,  d
endmodule
