// Logisim project MUX Project simult.circ as structural Verilog: 1 circuit, main circuit main
module main (
  input  [1:0] A_B,
  input  C,
  input  _0,
  input  _1
);

  wire multiplexer_1_out, multiplexer_2_out, multiplexer_3_out, multiplexer_4_out, multiplexer_5_out,
       multiplexer_6_out, not_1_out;

  not not_1 (not_1_out, C);
  Multiplexer #(.select(2)) multiplexer_1 (
    .in0(_1), .in1(_1), .in2(not_1_out), .in3(C), .out(multiplexer_1_out), .sel(A_B));  // open: en
  Multiplexer #(.select(2)) multiplexer_2 (
    .in0(_0), .in1(C), .in2(_1), .in3(C), .out(multiplexer_2_out), .sel(A_B));  // open: en
  Multiplexer #(.select(2)) multiplexer_3 (
    .in0(C), .in1(_0), .in2(_1), .in3(C), .out(multiplexer_3_out), .sel(A_B));  // open: en
  Multiplexer #(.select(2)) multiplexer_4 (
    .in0(not_1_out), .in1(_1), .in2(_0), .in3(_0), .out(multiplexer_4_out), .sel(A_B));  // open: en
  Multiplexer #(.select(2)) multiplexer_5 (
    .in0(_1), .in1(not_1_out), .in2(_0), .in3(C), .out(multiplexer_5_out), .sel(A_B));  // open: en
  Multiplexer #(.select(2)) multiplexer_6 (
    .in0(C), .in1(_1), .in2(not_1_out), .in3(_1), .out(multiplexer_6_out), .sel(A_B));  // open: en
  _7_Segment_Display u_7_segment_display_1 (
    .g(multiplexer_6_out), .f(multiplexer_5_out), .a(multiplexer_1_out), .b(multiplexer_2_out),
    .e(multiplexer_4_out), .d(multiplexer_1_out), .c(multiplexer_3_out));  // open: dp

  // Notes on the sheet:
  //   ( MSB )
  //   ( LSB )
  //   a   ,   d
  //   b
  //   c
  //   e
  //   f
  //   g
endmodule
