// Logisim project Sequencial MUX Project simult.circ as structural Verilog: 1 circuit, main circuit main
module main (
  input  _0,
  input  _1,
  output [2:0] A_B_C
);

  wire A_qn, and_1_out, and_2_out, and_3_out, and_4_out, and_5_out, B_qn, C_qn, clock_1_out,
       multiplexer_1_out, multiplexer_2_out, multiplexer_3_out, multiplexer_4_out, multiplexer_5_out,
       multiplexer_6_out, or_1_out, or_2_out;

  Clock clock_1 (.out(clock_1_out));
  and and_1 (and_1_out, A_B_C[2], A_B_C[2], B_qn);
  or or_1 (or_1_out, and_1_out, and_2_out, and_3_out);
  and and_2 (and_2_out, A_B_C[2], A_B_C[2], C_qn);
  and and_3 (and_3_out, A_qn, A_B_C[1], A_B_C[0]);
  and and_4 (and_4_out, A_B_C[1], A_B_C[1], C_qn);
  or or_2 (or_2_out, and_4_out, and_5_out, and_5_out);
  and and_5 (and_5_out, B_qn, A_B_C[0], A_B_C[0]);
  D_Flip_Flop A (.clk(clock_1_out), .D(or_1_out), .Q(A_B_C[2]), .Qn(A_qn));  // open: preset, en, reset
  D_Flip_Flop B (.clk(clock_1_out), .D(or_2_out), .Q(A_B_C[1]), .Qn(B_qn));  // open: preset, en, reset
  D_Flip_Flop C (.clk(clock_1_out), .D(C_qn), .Q(A_B_C[0]), .Qn(C_qn));  // open: preset, en, reset
  Multiplexer #(.select(2)) multiplexer_1 (
    .in0(_1), .in1(_1), .in2(C_qn), .in3(A_B_C[0]), .out(multiplexer_1_out), .sel(A_B_C[2:1]));  // open: en
  Multiplexer #(.select(2)) multiplexer_2 (
    .in0(_0), .in1(A_B_C[0]), .in2(_1), .in3(A_B_C[0]), .out(multiplexer_2_out), .sel(A_B_C[2:1]));  // open: en
  Multiplexer #(.select(2)) multiplexer_3 (
    .in0(A_B_C[0]), .in1(_0), .in2(_1), .in3(A_B_C[0]), .out(multiplexer_3_out), .sel(A_B_C[2:1]));  // open: en
  Multiplexer #(.select(2)) multiplexer_4 (
    .in0(C_qn), .in1(_1), .in2(_0), .in3(_0), .out(multiplexer_4_out), .sel(A_B_C[2:1]));  // open: en
  Multiplexer #(.select(2)) multiplexer_5 (
    .in0(_1), .in1(C_qn), .in2(_0), .in3(A_B_C[0]), .out(multiplexer_5_out), .sel(A_B_C[2:1]));  // open: en
  Multiplexer #(.select(2)) multiplexer_6 (
    .in0(A_B_C[0]), .in1(_1), .in2(C_qn), .in3(_1), .out(multiplexer_6_out), .sel(A_B_C[2:1]));  // open: en
  _7_Segment_Display u_7_segment_display_1 (
    .g(multiplexer_6_out), .f(multiplexer_5_out), .a(multiplexer_1_out), .b(multiplexer_2_out),
    .e(multiplexer_4_out), .d(multiplexer_1_out), .c(multiplexer_3_out));  // open: dp

  // Notes on the sheet:
  //   clk
  //   ( MSB )
  //   D FF
  //   ( LSB )
  //   A (t)
  //   B (t)
  //   C (t)
  //   C
  //   C'
  //   A B
  //   b
  //   c
  //   e
  //   f
  //   g
  //   a  ,  d
endmodule
