// Logisim project Universal gate Project simult.circ as structural Verilog: 1 circuit, main circuit main
module main (
  input  A,
  input  B,
  input  C
);

  wire nand_1_out, nand_2_out, nand_3_out, nand_4_out, nand_5_out, nand_6_out, nand_7_out, nand_8_out,
       nand_9_out, nand_10_out, nand_11_out, nand_12_out, nand_13_out, nand_14_out, nand_15_out, nand_16_out,
       nand_17_out, nand_18_out, nand_19_out, nand_20_out;

  nand nand_1 (nand_1_out, A, A);
  nand nand_2 (nand_2_out, B, B);
  nand nand_3 (nand_3_out, C, C);
  nand nand_4 (nand_4_out, B, C);
  nand nand_5 (nand_5_out, nand_2_out, nand_3_out);
  nand nand_6 (nand_6_out, A, nand_2_out);
  nand nand_7 (nand_7_out, A, C);
  nand nand_8 (nand_8_out, nand_2_out, C);
  nand nand_9 (nand_9_out, nand_1_out, B);
  nand nand_10 (nand_10_out, nand_1_out, nand_3_out);
  nand nand_11 (nand_11_out, nand_1_out, nand_2_out);
  nand nand_12 (nand_12_out, A, B, C);
  nand nand_13 (nand_13_out, nand_1_out, C);
  nand nand_14 (nand_14_out, A, nand_3_out);
  nand nand_15 (nand_15_out, nand_4_out, nand_5_out, A);
  nand nand_16 (nand_16_out, nand_6_out, nand_4_out);
  nand nand_17 (nand_17_out, nand_6_out, nand_7_out, nand_8_out);
  nand nand_18 (nand_18_out, nand_9_out, nand_10_out);
  nand nand_19 (nand_19_out, nand_10_out, nand_11_out, nand_12_out);
  nand nand_20 (nand_20_out, nand_13_out, nand_14_out, nand_2_out);
  _7_Segment_Display u_7_segment_display_1 (
    .g(nand_20_out), .f(nand_19_out), .a(nand_15_out), .b(nand_16_out), .e(nand_18_out), .d(nand_15_out),
    .c(nand_17_out));  // open: dp

  // Notes on the sheet:
  //   ( MSB )
  //   ( LSB )
  //   a  ,  d
  //   b
  //   c
  //   e
  //   f
  //   g
endmodule
